// Logisim project mm_interruptions_etu_2016_2017.circ as structural Verilog: 5 circuits, main circuit Von Neumann machine
module Von_Neumann_machine (
);

  wire clock_out, cpu_1_intack, cpu_1_m_we, or_1_out, press_here_to_request_an_interrupt_out, reset_out,
       s_r_ff_1_q;
  wire [7:0] cpu_1_ma, cpu_1_mdo, ram_1_data;

  CPU cpu_1 (
    .MA(cpu_1_ma), .MDI(ram_1_data), .MDO(cpu_1_mdo), .M_we(cpu_1_m_we), .ck(clock_out), .reset(reset_out),
    .IRQ(s_r_ff_1_q), .intACK(cpu_1_intack));
  Clock clock (.out(clock_out));
  Button reset (.out(reset_out));
  // Probe on cpu_1_ma
  // Probe on cpu_1_mdo
  // Probe on ram_1_data
  Button press_here_to_request_an_interrupt (.out(press_here_to_request_an_interrupt_out));
  or or_1 (or_1_out, cpu_1_intack, reset_out);
  S_R_Flip_Flop #(.trigger("high")) s_r_ff_1 (
    .S(press_here_to_request_an_interrupt_out), .clk(1'b1), .R(or_1_out), .Q(s_r_ff_1_q));  // open: Qn, preset, reset, en
  RAM #(.bus("separate")) ram_1 (
    .addr(cpu_1_ma), .din(cpu_1_mdo), .data(ram_1_data), .str(cpu_1_m_we), .sel(1'b1), .clk(clock_out),
    .ld(1'b1));  // open: clr

  // Notes on the sheet:
  //   Processor
  //   interrupt request
  //   interrupt acknowledgement
  //   address
  //   data: CPU to memory
  //   data: memory to CPU
  //   control: 1 means "write"
  //   Interrupt Controller
  //   Memory
endmodule

module CPU (
  input  IRQ,
  input  [7:0] MDI,
  input  ck,
  input  reset,
  output [7:0] MA,
  output [7:0] MDO,
  output M_we,
  output intACK
);

  wire fsm_1_p5, fsm_1_p6, fsm_1_p7, fsm_1_p8, fsm_1_p9, fsm_1_p10, fsm_1_p11, fsm_1_p12, fsm_1_p13,
       fsm_1_p14, fsm_1_p15, fsm_1_p16, fsm_1_p17;
  wire [2:0] fsm_1_p2;
  wire [7:0] fsm_1_p1;

  // FSM fsm_1: pin names not known; wires that end beside it: fsm_1_p1, fsm_1_p2, ck, reset, fsm_1_p5, fsm_1_p6, fsm_1_p7, fsm_1_p8, fsm_1_p9, fsm_1_p10, fsm_1_p11, fsm_1_p12, fsm_1_p13, fsm_1_p14, fsm_1_p15, fsm_1_p16, fsm_1_p17, M_we, intACK
  DataPath datapath_1 (
    .weIR(fsm_1_p5), .selMA(fsm_1_p6), .weDestReg(fsm_1_p7), .wePC(fsm_1_p8), .weCST(fsm_1_p9),
    .selPCJA(fsm_1_p10), .selPCJR(fsm_1_p11), .weFlags(fsm_1_p12), .MA(MA), .MDI(MDI), .MDO(MDO),
    .Flags(fsm_1_p2), .ck(ck), .reset(reset), .Instruction(fsm_1_p1), .restorePC(fsm_1_p13),
    .ceSavedFlags(fsm_1_p14), .ceSavedFlags_2(fsm_1_p15), .ceSavedFlags_3(fsm_1_p16), .routine(fsm_1_p17));

  // Notes on the sheet:
  //   FSM = Automate
  //   Data Path
  //   Instruction
  //   Flags
  //   (memory address)
  //   (data in from mem)
  //   (data out to mem)
  //   (memory write enable)
endmodule

module DataPath (
  input  weIR,
  input  selMA,
  input  weDestReg,
  input  wePC,
  input  weCST,
  input  selPCJA,
  input  selPCJR,
  input  weFlags,
  input  restorePC,
  input  ceSavedFlags,
  input  ceSavedFlags_2,
  input  ceSavedFlags_3,
  input  routine,
  input  [7:0] MDI,
  input  ck,
  input  reset,
  output [7:0] Instruction,
  output [7:0] MA,
  output [7:0] MDO,
  output [2:0] Flags
);

  wire comparator_1_eq, weA, weB;
  wire [2:0] alu_1_zcn, multiplexer_5_out, savedFlags;
  wire [7:0] adder_1_out, alu_1_out, multiplexer_2_out, multiplexer_3_out, multiplexer_4_out,
       multiplexer_6_out, multiplexer_7_out, multiplexer_8_out, regA, regB, regCST, regPC, savedPC;

  Multiplexer #(.width(8), .enable("false")) multiplexer_1 (.in0(regA), .in1(regB), .out(MDO), .sel(Instruction[1]));
  Multiplexer #(.width(8), .enable("false")) multiplexer_2 (
    .in0(regA), .in1(regCST), .out(multiplexer_2_out), .sel(Instruction[2]));
  // Probe on MDO
  // Probe on multiplexer_2_out
  Multiplexer #(.width(8), .enable("false")) multiplexer_3 (
    .in0(8'h1), .in1({{4{Instruction[4]}}, Instruction[3:0]}), .out(multiplexer_3_out), .sel(selPCJR));
  // Probe on alu_1_out
  ALU alu_1 (
    .arg1(MDO), .ZCN(alu_1_zcn), .out(alu_1_out), .arg2(multiplexer_2_out), .codeOp(Instruction[6:3]),
    .passtrough__invert(Instruction[2]));
  Adder adder_1 (.a(regPC), .b(multiplexer_3_out), .out(adder_1_out));  // open: cin, cout
  Register u_savedPC (.D(regPC), .en(ceSavedFlags_2), .Q(savedPC), .clk(ck));  // open: clr
  Multiplexer #(.width(8), .enable("false")) multiplexer_4 (
    .in0(adder_1_out), .in1(regCST), .out(multiplexer_4_out), .sel(selPCJA));
  Multiplexer #(.width(3), .enable("false")) multiplexer_5 (
    .in0(alu_1_zcn), .in1(savedFlags), .out(multiplexer_5_out), .sel(ceSavedFlags_3));
  Multiplexer #(.width(8), .enable("false")) multiplexer_6 (
    .in0(multiplexer_4_out), .in1(savedPC), .out(multiplexer_6_out), .sel(restorePC));
  // Probe on multiplexer_5_out
  Register #(.width(3)) u_savedFlags (.D(Flags), .en(ceSavedFlags), .Q(savedFlags), .clk(ck));  // open: clr
  // Probe on Flags
  Register #(.width(3)) u_flags (.D(multiplexer_5_out), .en(weFlags), .Q(Flags), .clk(ck), .clr(reset));
  Multiplexer #(.width(8), .enable("false")) multiplexer_7 (
    .in0(alu_1_out), .in1(MDI), .out(multiplexer_7_out), .sel(comparator_1_eq));
  Comparator #(.width(4)) comparator_1 (.a(Instruction[6:3]), .b(4'b1101), .eq(comparator_1_eq));  // open: gt, lt
  Multiplexer #(.width(8), .enable("false")) multiplexer_8 (
    .in0(multiplexer_6_out), .in1(8'h40), .out(multiplexer_8_out), .sel(routine));
  Register IR (.D(MDI), .en(weIR), .Q(Instruction), .clk(ck), .clr(reset));
  Register CST (.D(MDI), .en(weCST), .Q(regCST), .clk(ck), .clr(reset));
  // Probe on multiplexer_8_out
  Register PC (.D(multiplexer_8_out), .en(wePC), .Q(regPC), .clk(ck), .clr(reset));
  Register A (.D(multiplexer_7_out), .en(weA), .Q(regA), .clk(ck), .clr(reset));
  Register B (.D(multiplexer_7_out), .en(weB), .Q(regB), .clk(ck), .clr(reset));
  and and_1 (weA, ~Instruction[0], weDestReg);  // AND_Gate
  and and_2 (weB, Instruction[0], weDestReg);
  // Probe on multiplexer_2_out
  // Probe on MDI
  Multiplexer #(.width(8), .enable("false")) multiplexer_9 (
    .in0(multiplexer_2_out), .in1(regPC), .out(MA), .sel(selMA));

  // Other names for the same wires on the sheet: destS = Instruction[0]; offset[4:0] = Instruction[4:0];
  //   arg1S = Instruction[1]; arg2S = Instruction[2]; opcode[3:0] = Instruction[6:3]; ceSavedPC = ceSavedFlags_2;
  //   restoreFlags = ceSavedFlags_3

  // Notes on the sheet:
  //   (memory address)
  //   (data in from mem)
  //   (data out to mem)
endmodule

module ALU (
  input  [7:0] arg1,
  input  [7:0] arg2,
  input  [3:0] codeOp,
  input  passtrough__invert,
  output [2:0] ZCN,
  output [7:0] out
);

  wire carryAdd, carrySub;
  wire [7:0] adder_1_out, and_1_out, or_1_out, subtractor_1_out, xor_1_out, xor_2_out;

  // Probe on arg1
  // Probe on arg2
  Adder adder_1 (.a(arg1), .b(arg2), .out(adder_1_out), .cin(1'b0), .cout(carryAdd));
  Subtractor subtractor_1 (.a(arg1), .b(arg2), .out(subtractor_1_out), .bin(1'b0), .bout(carrySub));
  // Probe on adder_1_out
  // Probe on subtractor_1_out
  assign and_1_out = arg1 & arg2;  // AND_Gate and_1, 8 bits wide
  assign or_1_out = arg1 | arg2;  // OR_Gate or_1, 8 bits wide
  assign xor_1_out = arg1 ^ arg2;  // XOR_Gate xor_1, 8 bits wide
  assign xor_2_out = arg1 ^ {8{passtrough__invert}};  // XOR_Gate xor_2, 8 bits wide
  // Probe on out
  Multiplexer #(.select(4), .width(8), .enable("false")) multiplexer_1 (
    .in0(adder_1_out), .in1(subtractor_1_out), .in2(and_1_out), .in3(or_1_out), .in4(xor_1_out),
    .in5({1'b0, arg1[7:1]}), .in6(subtractor_1_out), .in8(xor_2_out), .in9(arg2), .out(out), .sel(codeOp));  // open: in7, in10, in11, in12, in13, in14, in15
  nor nor_1 (ZCN[2], out[0], out[1], out[2], out[3], out[4], out[5], out[6], out[7]);
  Multiplexer #(.select(3), .disabled(0), .enable("false")) multiplexer_2 (
    .in0(carryAdd), .in1(carrySub), .in5(arg1[0]), .in6(carrySub), .out(ZCN[1]), .sel(codeOp[2:0]));  // open: in2, in3, in4, in7

  assign ZCN[0] = out[7];

  // Notes on the sheet:
  //   0000 add
  //   0001 sub
  //   0010 and
  //   0011 or
  //   0100 xor
  //   0110 cmp
  //   0101 lsr
  //   1000 passthrough/invert arg1
  //   1001 passthrough arg2
  //   (only meaningful for the "1000" operation. zero is"passtrough" / one is "invert")
endmodule

module FSM (
  input  [7:0] Instruction,
  input  [2:0] flags,
  input  clk,
  input  reset,
  output weIR,
  output selMA,
  output weDestReg,
  output wePC,
  output weCST,
  output selPCJA,
  output selPCJR,
  output weFlags,
  output memwrite,
  output intAck,
  output restorePC,
  output ceSavedFlags,
  output ceSavedFlags_2,
  output ceSavedFlags_3,
  output routine
);

  wire and_1_out, and_2_out, and_3_out, and_4_out, and_5_out, and_6_out, and_7_out, and_8_out, and_9_out,
       and_10_out, and_11_out, and_12_out, and_13_out, instr_is_add, instr_is_ALU, instr_is_and,
       instr_is_cmp, instr_is_JA, instr_is_lsr, instr_is_MEM, instr_is_memload, instr_is_memstore,
       instr_is_one_word, instr_is_or, instr_is_pass1, instr_is_pass2, instr_is_sub, instr_is_xor,
       jump_cond_is_true, not_1_out, or_1_out, or_5_out, or_6_out, or_7_out, or_8_out, or_9_out,
       state_dontJR, state_IncrPC, state_InstrDecode, state_ReadMem, state_RegNoWrite, state_RegWrite;

  Demultiplexer #(.select(4), .enable("false")) demultiplexer_1 (
    .out0(instr_is_add), .out1(instr_is_sub), .out2(instr_is_and), .out3(instr_is_or), .out4(instr_is_xor),
    .out5(instr_is_lsr), .out6(instr_is_cmp), .out8(instr_is_pass1), .out9(instr_is_pass2),
    .out13(instr_is_memload), .out14(instr_is_memstore), .out15(instr_is_JA), .in(not_1_out),
    .sel(Instruction[6:3]));  // open: out7, out10, out11, out12
  not not_1 (not_1_out, Instruction[7]);
  // Probe on Instruction
  Multiplexer #(.select(2), .enable("false")) multiplexer_1 (
    .in0(1'b1), .in1(flags[2]), .in2(flags[1]), .in3(flags[0]), .out(jump_cond_is_true),
    .sel(Instruction[6:5]));
  or or_1 (or_1_out, instr_is_ALU, instr_is_MEM);
  and and_1 (and_1_out, or_1_out, ~Instruction[2]);  // AND_Gate
  or or_2 (instr_is_one_word, Instruction[7], instr_is_pass1, and_1_out);
  or or_3 (instr_is_ALU, instr_is_add, instr_is_sub, instr_is_and, instr_is_or, instr_is_xor, instr_is_lsr, instr_is_cmp, instr_is_pass1, instr_is_pass2);
  or or_4 (instr_is_MEM, instr_is_memload, instr_is_memstore);
  or or_5 (or_5_out, state_RegWrite, selPCJR, selPCJA, state_RegNoWrite, state_dontJR, memwrite, state_ReadMem);
  and and_2 (and_2_out, weCST, instr_is_JA);
  and and_3 (and_3_out, state_InstrDecode, instr_is_one_word, instr_is_ALU, ~instr_is_cmp);  // AND_Gate
  and and_4 (and_4_out, weCST, ~instr_is_JA);  // AND_Gate
  and and_5 (and_5_out, state_InstrDecode, instr_is_one_word, instr_is_cmp);
  and and_6 (and_6_out, weCST, instr_is_cmp);
  and and_7 (and_7_out, state_InstrDecode, instr_is_one_word, instr_is_memload);
  and and_8 (and_8_out, weCST, instr_is_memload);
  and and_9 (and_9_out, state_InstrDecode, instr_is_one_word, instr_is_memstore);
  and and_10 (and_10_out, weCST, instr_is_memstore);
  and and_11 (and_11_out, state_InstrDecode, ~instr_is_one_word);  // AND_Gate
  or or_6 (or_6_out, and_3_out, and_4_out);
  or or_7 (or_7_out, and_5_out, and_6_out);
  and and_12 (and_12_out, state_InstrDecode, Instruction[7], jump_cond_is_true);
  and and_13 (and_13_out, state_InstrDecode, Instruction[7], ~jump_cond_is_true);  // AND_Gate
  or or_8 (or_8_out, and_7_out, and_8_out);
  or or_9 (or_9_out, and_9_out, and_10_out);
  D_Flip_Flop d_ff_1 (.clk(clk), .D(or_5_out), .Q(weIR), .preset(reset));  // open: Qn, en, reset
  D_Flip_Flop d_ff_2 (.clk(clk), .D(weIR), .Q(state_InstrDecode), .reset(reset));  // open: Qn, preset, en
  D_Flip_Flop d_ff_3 (.clk(clk), .D(and_11_out), .Q(state_IncrPC), .reset(reset));  // open: Qn, preset, en
  D_Flip_Flop d_ff_4 (.clk(clk), .D(state_IncrPC), .Q(weCST), .reset(reset));  // open: Qn, preset, en
  D_Flip_Flop d_ff_5 (.clk(clk), .D(and_2_out), .Q(selPCJA), .reset(reset));  // open: Qn, preset, en
  D_Flip_Flop d_ff_6 (.clk(clk), .D(or_6_out), .Q(state_RegWrite), .reset(reset));  // open: Qn, preset, en
  D_Flip_Flop d_ff_7 (.clk(clk), .D(or_7_out), .Q(state_RegNoWrite), .reset(reset));  // open: Qn, preset, en
  D_Flip_Flop d_ff_8 (.clk(clk), .D(and_12_out), .Q(selPCJR), .reset(reset));  // open: Qn, preset, en
  D_Flip_Flop d_ff_9 (.clk(clk), .D(and_13_out), .Q(state_dontJR), .reset(reset));  // open: Qn, preset, en
  D_Flip_Flop d_ff_10 (.clk(clk), .D(or_8_out), .Q(state_ReadMem), .reset(reset));  // open: Qn, preset, en
  D_Flip_Flop d_ff_11 (.clk(clk), .D(or_9_out), .Q(memwrite), .reset(reset));  // open: Qn, preset, en
  or or_10 (selMA, weIR, weCST);
  or or_11 (weDestReg, state_RegWrite, state_ReadMem);
  or or_12 (weFlags, state_RegWrite, state_RegNoWrite);
  or or_13 (wePC, state_RegWrite, selPCJR, state_IncrPC, selPCJA, state_RegNoWrite, state_dontJR, memwrite, state_ReadMem);

  // Other names for the same wires on the sheet: ceSavedPC = ceSavedFlags_2; arg2S = Instruction[2];
  //   instr_is_JR = Instruction[7]; opcode[3:0] = Instruction[6:3]; jump_cond[1:0] = Instruction[6:5];
  //   restoreFlags = ceSavedFlags_3; state_CstFetch = weCST; state_doJA = selPCJA; state_doJR = selPCJR;
  //   state_InstrFetch = weIR; state_WriteMem = memwrite

  // Notes on the sheet:
  //   Z C N
  //   TODO....
endmodule
